# Fritzing sketch Steckplan (saved by Fritzing 1.0.4)
breadboards: 1

parts:
  Bauteil97 = ESP32-C6 Dev Kit N8
  Bauteil98 = BH1750

nets:
  3V3: Bauteil97.10, Bauteil97.3V3, Bauteil97.23, Bauteil98.VCC
  N1: Bauteil97.8, Bauteil97.RST, Bauteil97.TX, Bauteil97.22
  N2: Bauteil97.7, Bauteil98.SCL
  N3: Bauteil97.6, Bauteil98.SDA
  N4: Bauteil97.GND#15, Bauteil98.GND

custom parts:
  ESP32-C6 Dev Kit N8: ESP32-C6-N8
  BH1750: Light Sensor
