# Fritzing sketch Steckplan (saved by Fritzing 1.0.4)
breadboards: 1

parts:
  Bauteil99 = ESP32-C6 Dev Kit N8
  Bauteil100 = MQ-3 breakout  # not connected

nets:
  N1: Bauteil99.10, Bauteil99.3V3, Bauteil99.23
  N2: Bauteil99.8, Bauteil99.RST, Bauteil99.TX, Bauteil99.22

custom parts:
  ESP32-C6 Dev Kit N8: ESP32-C6-N8
  MQ-3 breakout: Alcohol sensor is capable of detecting alcohol (ethanol) particles on itself and gives the information in digital form back to us to manipulate with it. SKU:101251 • Voltage: 5V DC • Power: max 750mW • Measurement range: 0.04-4mg/L
