# Fritzing sketch Steckplan (saved by Fritzing 1.0.4)
breadboards: 1

parts:
  Bauteil100 = ESP32-C6 Dev Kit N8
  S23 = SCD40 - 4 pins [package="SIP (Single Inline) [THT]"]

nets:
  3V3: Bauteil100.10, Bauteil100.3V3, Bauteil100.23, S23.VDD
  N1: Bauteil100.8, Bauteil100.RST, Bauteil100.TX, Bauteil100.22
  N2: Bauteil100.7, S23.SCL
  N3: Bauteil100.6, S23.SDA
  N4: Bauteil100.GND#15, S23.GND

custom parts:
  ESP32-C6 Dev Kit N8: ESP32-C6-N8
