# Fritzing sketch mic (saved by Fritzing 1.0.4)
breadboards: 1

parts:
  Bauteil93 = ESP32-C6 Dev Kit N8
  Bauteil94 = INMP441

nets:
  N1: Bauteil93.2, Bauteil94.SCK
  3V3: Bauteil93.10, Bauteil93.3V3, Bauteil93.23, Bauteil94.WS, Bauteil94.VDD
  N2: Bauteil93.8, Bauteil93.RST, Bauteil93.TX, Bauteil93.22
  N3: Bauteil93.GND#15, Bauteil94.L/R, Bauteil94.GND
  N4: Bauteil93.13, Bauteil94.SD

custom parts:
  ESP32-C6 Dev Kit N8: ESP32-C6-N8
  INMP441: This is a simple breakout board for the INMP441 I2S MEMS microphone.
