# Fritzing sketch Steckplan (saved by Fritzing 1.0.4)
breadboards: 1

parts:
  Bauteil95 = ESP32-C6 Dev Kit N8
  Bauteil96 = sensor_biometrico

nets:
  N1: Bauteil95.GND#0, Bauteil96.GND
  3V3: Bauteil95.10, Bauteil95.3V3, Bauteil95.23, Bauteil96.VCC
  N2: Bauteil95.8, Bauteil95.RST, Bauteil95.TX, Bauteil95.22
  N3: Bauteil95.7, Bauteil96.RX
  N4: Bauteil95.6, Bauteil96.TX

custom parts:
  ESP32-C6 Dev Kit N8: ESP32-C6-N8
  sensor_biometrico: Adafruit Optical Fingerprint Sensor
