# Fritzing sketch Steckplan (saved by Fritzing 1.0.4)
breadboards: 1

parts:
  MP3-2 = Serial MP3 Player
  Q2 = TRANSISTOR_NPN [package=to-92-ammo]
  Bauteil91 = ESP32-C6 Dev Kit N8
  S12 = Pushbutton [package="[THT]"]

nets:
  N1: MP3-2.pin1, Q2.C
  N2: MP3-2.pin2, Bauteil91.3
  N3: MP3-2.pin3, Bauteil91.6
  N4: MP3-2.pin4, Bauteil91.5
  N5: Q2.E, Bauteil91.5V
  N6: Q2.B, Bauteil91.4
  N7: Bauteil91.10, Bauteil91.3V3, Bauteil91.23
  N8: Bauteil91.8, Bauteil91.RST, Bauteil91.TX, Bauteil91.22
  N9: Bauteil91.RX, S12.Pin_3, S12.Pin_4
  N10: S12.Pin_1, S12.Pin_2

custom parts:
  Serial MP3 Player: The module is a kind of simple MP3 player device which is based on a high-quality MP3 audio chip---YX5300. It can support 8k Hz ~ 48k Hz sampling frequency MP3 and WAV file formats. There is a TF card socket on board, so you can plug the micro SD card that stores audio files. MCU can control the MP3 playback state by sending commands to the module via UART port, such as switch songs, change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
  ESP32-C6 Dev Kit N8: ESP32-C6-N8
