# Fritzing sketch Wägesensor+HX711 (saved by Fritzing 1.0.4)
breadboards: 1

parts:
  Load_Cell3 = Load Cell - Red/white/black/green  # not connected
  Part5 = HX711 Weighing Sensor Module  # not connected
  Bauteil61 = ESP32-C6 Dev Kit N8

nets:
  N1: Bauteil61.10, Bauteil61.3V3, Bauteil61.23
  N2: Bauteil61.8, Bauteil61.RST, Bauteil61.TX, Bauteil61.22

custom parts:
  Load Cell - Red/white/black/green: A rectangle load cell/weighting pressure Sensor with four wires - Red, white, black, green. Normally corresponding with E+, E-, A+, A- respectively.
  HX711 Weighing Sensor Module: HX711 is a precision 24-bit analog-to-digital converter (ADC) designed for weigh scales and industrial control applications to interface directly with a bridge sensor.
  ESP32-C6 Dev Kit N8: ESP32-C6-N8
