# Fritzing sketch rpi_ledring (saved by Fritzing 1.0.4)

parts:
  Mod1 = Raspberry Pi 4B
  A1 = Raspberry Pi 5
  Bauteil1 = 12 NeoPixel Ring [part_number=1643]
  Bauteil2 = 12 NeoPixel Ring [part_number=1643]
  Bauteil70 = 12 NeoPixel Ring [part_number=1643]
  Bauteil71 = ESP32-C6 Dev Kit N8

nets:
  5V: Mod1.5V, Bauteil2.VDD
  GND: Mod1.GND, Bauteil2.GND
  N1: Mod1.GPIO18, Bauteil2.IN
  5V_2: A1.5V, Bauteil1.VDD
  GND_2: A1.GND, Bauteil1.GND
  N2: A1.GPIO10, Bauteil1.IN
  N3: Bauteil70.IN, Bauteil71.2
  GND_3: Bauteil70.GND, Bauteil71.GND
  VDD: Bauteil70.VDD, Bauteil71.5V

custom parts:
  Raspberry Pi 5: The RPi5, a faster version of the awesome Raspberry Pi4B ARM Board with 40 pin gpio.
  12 NeoPixel Ring: 12 ultra bright smart LED NeoPixels are arranged in a circle with 1.5" (37mm) outer diameter. The rings are 'chainable' - connect the output pin of one to the input pin of another. Use only one microcontroller pin to control as many as you can chain together! Each LED is addressable as the driver chip is inside the LED. Each one has ~18mA constant current drive so the color will be very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
  ESP32-C6 Dev Kit N8: ESP32-C6-N8
